# Fritzing sketch NodeMCU_LED (saved by Fritzing 0.9.3b)
breadboards: 1

parts:
  LED1 = LED - 5mm [color="Red (633nm)" package="5 mm [THT]"]
  U1 = NodeMCU V3.0
  R2 = Resistor [tolerance=±5% resistance=220 package=THT]

nets:
  N1: LED1.cathode, R2.Pin_1
  N2: LED1.anode, U1.D2
  N3: U1.GND, R2.Pin_0

custom parts:
  NodeMCU V3.0: ESP8266 based NodeMCU
