# Fritzing sketch NodeMCU_Ultrasonic (saved by Fritzing 0.9.3b)

parts:
  U1 = NodeMCU V3.0
  HC-SR04_Sensor_1 = HC-SR04 Ultrasonic Distance Sensor
  J1 = Piezo Speaker

nets:
  GND: U1.GND, HC-SR04_Sensor_1.GND, J1.pin1
  N1: U1.D5, HC-SR04_Sensor_1.TRIG
  N2: U1.D6, HC-SR04_Sensor_1.ECHO
  N3: U1.D7, J1.pin2
  N4: U1.VU, HC-SR04_Sensor_1.VCC

custom parts:
  NodeMCU V3.0: ESP8266 based NodeMCU
