# Fritzing sketch Arduino_LED_HC05 (saved by Fritzing 0.9.3b)

parts:
  Part1 = Bluetooth HC-05 Macho
  USBUART1 = CP2102 USB UART Breakout
  Part3 = Arduino Uno (Rev3)
  LED2 = smd LED [color="Red (633nm)" package="0805 [SMD]"]
  Part4 = Bluetooth HC-05 Macho

nets:
  N1: Part1.TXD, USBUART1.RXD
  N2: Part1.RXD, USBUART1.TXD
  N3: Part1.VCC, USBUART1.VCCIO
  GND: Part1.GND, USBUART1.GND
  N4: Part3.D13/SCK, LED2.anode
  GND_2: Part3.GND, LED2.cathode, Part4.GND
  N5: Part3.D0/RX, Part4.TXD
  N6: Part3.D1/TX, Part4.RXD
  5V: Part3.5V, Part4.VCC

custom parts:
  CP2102 USB UART Breakout: CP2102 Usb Uart Breakout Board with Battery
