# Fritzing sketch TTL_HC05 (saved by Fritzing 0.9.3b)

parts:
  Part1 = Bluetooth HC-05 Macho
  USBUART1 = CP2102 USB UART Breakout

nets:
  N1: Part1.TXD, USBUART1.RXD
  N2: Part1.RXD, USBUART1.TXD
  N3: Part1.VCC, USBUART1.VCCIO
  GND: Part1.GND, USBUART1.GND

custom parts:
  CP2102 USB UART Breakout: CP2102 Usb Uart Breakout Board with Battery
