# Fritzing sketch Arduino_HC05 (saved by Fritzing 0.9.3b)

parts:
  Part1 = Arduino Uno (Rev3)
  Part2 = Bluetooth HC-05 Macho
  C1 = Electrolytic Capacitor [capacitance=10µF voltage=6.3V package="0405 [SMD, electrolytic]"]
  LED1 = LED - 5mm [color="Red (633nm)" package="5 mm [THT]"]

nets:
  N1: Part1.D9_PWM, LED1.anode
  GND: Part1.GND, Part2.GND, LED1.cathode
  N2: Part1.D0/RX, Part2.TXD
  N3: Part1.D1/TX, Part2.RXD
  N4: Part1.RESET, C1.-
  5V: Part1.5V, Part2.VCC
  N5: Part2.State, C1.+

notes:
  Connect to a remote Power Source (not PC)
