# Fritzing sketch NodeMCU_LED (saved by Fritzing 0.9.3b)

parts:
  U2 = NodeMCU V3.0
  LED2 = LED - 5mm [color="Red (633nm)" package="5 mm [THT]"]

nets:
  N1: U2.D4, LED2.anode
  N2: U2.GND, LED2.cathode

custom parts:
  NodeMCU V3.0: ESP8266 based NodeMCU
