# Fritzing sketch NodeMCU_Relay (saved by Fritzing 0.9.3b)

parts:
  KY-1 = Keyes Relay [package=THT]
  J1 = Camdenboss CTB0158-2 [part_number=CTB0158-2 package=THT]
  U1 = NodeMCU V3.0
  LED1 = LEDs [package=led10mm]

nets:
  N1: KY-1.signal, U1.D1
  N2: KY-1.power, U1.3V3
  N3: KY-1.ground, U1.GND
  N4: KY-1.NC, LED1.A
  N5: KY-1.C, J1.terminal_1
  N6: J1.terminal_2, LED1.C

notes:
  Two pin plug

custom parts:
  Keyes Relay: The Keyes 5V relay module is suitable for SCM development, home appliance control. It uses a 5V~12V TIL control signal which can control DC / AC signal.
  NodeMCU V3.0: ESP8266 based NodeMCU
  LEDs: LEDs Standard schematic elements and footprints for 5mm, 3mm, 1206, and 0603 sized LEDs. 5mm - Spark Fun Electronics SKU : COM-00529 (and others)
