# Fritzing sketch NodeMCU_SM_DHT_Rain (saved by Fritzing 0.9.3b)
breadboards: 1

parts:
  Mod1 = KY-015 Temperature & Humidity Sensor Module [package="Breakout board"]
  YL-83_-_Detection_Board1 = YL-83 Rain Sensor - Detection Board
  YL-83_-_Control_Board1 = YL-83 Rain Sensor - Control Board
  Part1 = FC-28 Soil Hygrometer Module - Probe
  U1 = NodeMCU V3.0
  WATER_PUMP1 = water pump/motor
  KY-1 = Keyes Relay [package=THT]
  VCC1 = Battery block 9V
  C3 = Ceramic Capacitor [capacitance="100 nF" package="1206 [SMD, multilayer]"]
  C4 = Ceramic Capacitor [package="1206 [SMD, multilayer]"]
  YL-83_-_Control_Board2 = YL-83 Rain Sensor - Control Board
  U2 = Voltage Regulator - 5V [package="TO220 [THT]"]

nets:
  N1: Mod1.S, U1.D3
  VCC: Mod1.Vin, YL-83_-_Control_Board1.VCC, U1.3V3, KY-1.power, YL-83_-_Control_Board2.VCC
  GND: Mod1.-, YL-83_-_Control_Board1.GND, U1.GND, KY-1.ground, YL-83_-_Control_Board2.GND
  N2: YL-83_-_Detection_Board1.POS, YL-83_-_Control_Board2.POS
  N3: YL-83_-_Detection_Board1.NEG, YL-83_-_Control_Board2.NEG
  N4: YL-83_-_Control_Board1.AO, U1.A0
  N5: YL-83_-_Control_Board1.POS, Part1.POS
  N6: YL-83_-_Control_Board1.NEG, Part1.NEG
  N7: U1.D1, KY-1.signal
  N8: U1.D2, YL-83_-_Control_Board2.DO
  N9: WATER_PUMP1.pin_1, VCC1.-, C3.1, C4.0, U2.GND
  N10: WATER_PUMP1.pin_2, KY-1.C
  N11: KY-1.NC, C3.0, U2.output_voltage
  N12: VCC1.+, C4.1, U2.input_voltage

custom parts:
  KY-015 Temperature & Humidity Sensor Module: KY-015 temperature and humidity sensor module, provides a low-latency serial interface to measure humidity and temperature.
  YL-83 Rain Sensor - Detection Board: The YL-83 is a rain sensor that has more resistance when dry and less resistance when wet. The module runs at 5V.
  YL-83 Rain Sensor - Control Board: The YL-83 is a rain sensor that has more resistance when dry and less resistance when wet. The module runs at 5V.
  FC-28 Soil Hygrometer Module - Probe: The FC-28 is a soil hygrometer module that uses the Texas Instruments LM393 comparator chip to provide an analog measurement of soil humidity.
  NodeMCU V3.0: ESP8266 based NodeMCU
  water pump/motor: WATER PUMP BY ARDUBLOCKTR
  Keyes Relay: The Keyes 5V relay module is suitable for SCM development, home appliance control. It uses a 5V~12V TIL control signal which can control DC / AC signal.
  Ceramic Capacitor: 330 nF multilayered Ceramic Capacitor
