# Fritzing sketch NodeMCU_LED (saved by Fritzing 0.9.3b)

parts:
  U1 = NodeMCU V3.0
  LED1 = LED - 3mm [color="Red (633nm)" package="3 mm [THT]"]

nets:
  N1: U1.GND, LED1.cathode
  N2: U1.D5, LED1.anode

custom parts:
  NodeMCU V3.0: ESP8266 based NodeMCU
