# Fritzing sketch NodeMCU_LDR_Laser (saved by Fritzing 0.9.3b)
breadboards: 1

parts:
  U1 = NodeMCU V3.0
  KY-008_Laserdiode1 = Laser [part_number=1219301 package=keys]
  VCC1 = 4 x AAA Battery Mount
  J1 = Piezo Speaker
  R4 = Photocell (LDR) [package=THT]
  R6 = Resistor [tolerance=±5% resistance=1k package=THT]
  S1 = Round Pushbutton

nets:
  N1: U1.GND#6, U1.GND#33, J1.pin1
  N2: U1.D5, J1.pin2
  N3: U1.3V3, R4.pin_0
  N4: U1.GND#41, R6.Pin_1
  N5: U1.A0, R4.pin_1, R6.Pin_0
  N6: KY-008_Laserdiode1.connector0pin, KY-008_Laserdiode1.connector1pin, S1.leg0
  N7: KY-008_Laserdiode1.connector2pin, VCC1.-
  N8: VCC1.+, S1.leg1

custom parts:
  NodeMCU V3.0: ESP8266 based NodeMCU
  Laser: KEYES KY-008 650nm Laser Transmitter Module
