# Fritzing sketch Arduino_RTC_OLED (saved by Fritzing 0.9.3b)
breadboards: 1

parts:
  Squix1 = OLED 0.96" 128x64 I2C SSD1306
  ZS-042_RTC1 = ZS-042 RTC Module
  J1 = Piezo Speaker
  Part1 = Arduino Uno (Rev3) - ICSP
  S1 = Momentary Switch [package=ksa_sealed_tac_switch]
  S2 = Momentary Switch [package=ksa_sealed_tac_switch]
  R1 = Resistor [tolerance=±5% resistance=1k package="0402 [SMD]"]
  R2 = Resistor [tolerance=±5% resistance=1k package="0402 [SMD]"]

nets:
  VCC: Squix1.VCC, ZS-042_RTC1.VCC, Part1.5V, S1.4, S2.2
  GND: Squix1.GND, ZS-042_RTC1.GND, J1.pin1, Part1.GND, R1.Pin_1, R2.Pin_0
  N1: Squix1.SCL, ZS-042_RTC1.SCL, Part1.A5/SCL
  N2: Squix1.SCA, ZS-042_RTC1.SDA, Part1.A4/SDA
  N3: J1.pin2, Part1.D4
  N4: Part1.D2, S1.1
  N5: Part1.D3_PWM, S2.3
  N6: S1.2, R1.Pin_0
  N7: S2.4, R2.Pin_1
