# Fritzing sketch Arduino_TCS3200_OLED (saved by Fritzing 0.9.3b)
breadboards: 1

parts:
  Squix1 = OLED 0.96" 128x64 I2C SSD1306
  Part1 = Arduino Uno (Rev3) - ICSP
  e-radionica1 = TCS230 Color Sensor [part_number=101209]

nets:
  VCC: Squix1.VCC, Part1.5V, e-radionica1.Vcc
  GND: Squix1.GND, Part1.GND, e-radionica1.Gnd
  N1: Squix1.SCL, Part1.A5/SCL
  N2: Squix1.SCA, Part1.A4/SDA
  N3: Part1.D2, e-radionica1.S0
  N4: Part1.D3_PWM, e-radionica1.S1
  N5: Part1.D4, e-radionica1.S2
  N6: Part1.D5_PWM, e-radionica1.S3
  N7: Part1.D7, e-radionica1.Out

custom parts:
  TCS230 Color Sensor: TCS230
