# Fritzing sketch MAX30100-02_OLED (saved by Fritzing 0.9.3b)
breadboards: 1

parts:
  M1 = MAX30102
  Part1 = Arduino Uno (Rev3)
  Squix1 = OLED 0.96" 128x64 I2C SSD1306
  J1 = Piezo Speaker
  R1 = Resistor [tolerance=±5% resistance=4.7k package="0603 [SMD]"]
  R2 = Resistor [tolerance=±5% resistance=4.7k package="0603 [SMD]"]

nets:
  VIN: M1.VIN, Part1.5V, Squix1.VCC
  N1: M1.SCL, Part1.A5/SCL, Squix1.SCL, R1.Pin_0
  N2: M1.SDA, Part1.A4/SDA, Squix1.SCA, R2.Pin_0
  GND: M1.GND, Part1.GND, Squix1.GND, J1.pin1
  N3: Part1.D2, J1.pin2
  N4: Part1.3V3, R1.Pin_1, R2.Pin_1

custom parts:
  MAX30102: Oximeter module using the MAX30102 chip. You may wish to read (and check your module) this post on power problems with these modules: https://reedpaper.wordpress.com/2018/08/22/pulse-oximeter-max30100-max30102-how-to-fix-wrong-board/ . As usual, if you want the mounting holes in pcb, you need to drag a hole over the pad in silkscreen to actually drill the hole (by default they are not drilled)
