# Fritzing sketch ArduinoBoard_wCP2102 (saved by Fritzing 0.9.3b)
breadboards: 1

parts:
  C2 = Ceramic Capacitor [capacitance=0.1nF package="100 mil [THT, multilayer]"]
  XTAL1 = Crystal [frequency="16 Mhz" package=SMD]
  U1 = ATmega 328P [package=dip]
  Part1 = USB converter CP2102
  C8 = Ceramic Capacitor [capacitance=22pF rated_voltage=35V package="200 mil [THT, multilayer]"]
  C9 = Ceramic Capacitor [capacitance=22pF rated_voltage=35V package="200 mil [THT, multilayer]"]
  S1 = Momentary Switch [package=ksa_sealed_tac_switch]
  LED1 = LED - 5mm [color="Orange (620nm)" package="5 mm [THT]"]
  R1 = Resistor [tolerance=±5% resistance=220 package=THT]
  LED3 = LED - 5mm [color="Green (555nm)" package="5 mm [THT]"]
  R2 = Resistor [tolerance=±5% resistance=220 package=THT]

nets:
  N1: C2.0, Part1.DTR
  N2: C2.1, U1.PC6_(PCINT14/^RESET)_[RESET], S1.2
  N3: XTAL1.pin_0, U1.PB6_(PCINT6/XTAL1/TOSC1)_[XTAL1], C9.0
  N4: XTAL1.pin_1, U1.PB7_(PCINT7/XTAL2/TOSC2)_[XTAL2], C8.0
  N5: U1.PD0_(PCINT16/RXD)_[D0], Part1.TXO
  N6: U1.PD1_(PCINT17/TXD)_[D1], Part1.RXI
  VCC: U1.VCC, U1.AVCC, U1.AREF, Part1.+5V, LED3.anode
  GND: U1.GND, Part1.GND, C8.1, C9.1, S1.4, R1.Pin_0, R2.Pin_0
  N7: U1.PB5_(SCK/PCINT5)_[D13], LED1.anode
  N8: LED1.cathode, R2.Pin_1
  N9: R1.Pin_1, LED3.cathode

custom parts:
  ATmega 328P: Atmel ATmega 328P-PU Microcontroller
