# Fritzing sketch ArduinoBoard_woCP2102 (saved by Fritzing 0.9.3b)
breadboards: 1

parts:
  XTAL1 = Crystal [frequency="16 Mhz" package=SMD]
  U1 = ATmega 328P [package=dip]
  C8 = Ceramic Capacitor [capacitance=22pF rated_voltage=35V package="200 mil [THT, multilayer]"]
  C9 = Ceramic Capacitor [capacitance=22pF rated_voltage=35V package="200 mil [THT, multilayer]"]
  S1 = Momentary Switch [package=ksa_sealed_tac_switch]
  LED1 = LED - 5mm [color="Orange (620nm)" package="5 mm [THT]"]
  R1 = Resistor [tolerance=±5% resistance=220 package=THT]
  LED3 = LED - 5mm [color="Green (555nm)" package="5 mm [THT]"]
  R2 = Resistor [tolerance=±5% resistance=220 package=THT]
  C11 = Ceramic Capacitor [capacitance=100nF package="100 mil [THT, multilayer]"]
  BAT1 = BC9VPC [package=bc9vpc]
  U3 = Voltage Regulator - 5V [package="TO220 [THT]"]
  C13 = Ceramic Capacitor [package="1206 [SMD, multilayer]"]

nets:
  N1: XTAL1.pin_0, U1.PB6_(PCINT6/XTAL1/TOSC1)_[XTAL1], C9.0
  N2: XTAL1.pin_1, U1.PB7_(PCINT7/XTAL2/TOSC2)_[XTAL2], C8.0
  N3: U1.PC6_(PCINT14/^RESET)_[RESET], S1.2
  N4: U1.VCC, U1.AVCC, U1.AREF, LED3.anode, C11.1, U3.output_voltage
  GND: U1.GND, C8.1, C9.1, S1.4, R1.Pin_0, R2.Pin_0, C11.0, BAT1.V-, U3.GND, C13.1
  N5: U1.PB5_(SCK/PCINT5)_[D13], LED1.anode
  N6: LED1.cathode, R2.Pin_1
  N7: R1.Pin_1, LED3.cathode
  N8: BAT1.V+, U3.input_voltage, C13.0

custom parts:
  ATmega 328P: Atmel ATmega 328P-PU Microcontroller
  Ceramic Capacitor: 330 nF multilayered Ceramic Capacitor
