# Fritzing sketch ArduinoUno_Bootloader (saved by Fritzing 0.9.3b)
breadboards: 1

parts:
  XTAL1 = Crystal [frequency="16 Mhz" package=SMD]
  U1 = ATmega 328P [package=dip]
  C8 = Ceramic Capacitor [capacitance=22pF rated_voltage=35V package="200 mil [THT, multilayer]"]
  C9 = Ceramic Capacitor [capacitance=22pF rated_voltage=35V package="200 mil [THT, multilayer]"]
  R2 = Resistor [tolerance=±5% resistance=10k package=THT]
  Part1 = Arduino Uno (Rev3)

nets:
  N1: XTAL1.pin_0, U1.PB6_(PCINT6/XTAL1/TOSC1)_[XTAL1], C8.0
  N2: XTAL1.pin_1, U1.PB7_(PCINT7/XTAL2/TOSC2)_[XTAL2], C9.0
  N3: U1.PC6_(PCINT14/^RESET)_[RESET], R2.Pin_0, Part1.D10_PWM/SS
  VCC: U1.VCC, U1.AVCC, R2.Pin_1, Part1.5V
  GND: U1.GND, C8.1, C9.1, Part1.GND
  N4: U1.PB3_(MOSI/OC2A/PCINT3)_[D11_PWM], Part1.D11_PWM/MOSI
  N5: U1.PB4_(MISO/PCINT4)_[D12], Part1.D12/MISO
  N6: U1.PB5_(SCK/PCINT5)_[D13], Part1.D13/SCK

custom parts:
  ATmega 328P: Atmel ATmega 328P-PU Microcontroller
