# Fritzing sketch NodeMCU_RFID_RTC (saved by Fritzing 0.9.3b)
breadboards: 1

parts:
  U1 = NodeMCU V3.0
  J1 = Piezo Speaker
  Part1 = RFID-RC522-v2
  LED1 = smd LED [color="Green (555nm)" package="0805 [SMD]"]
  ZS-042_RTC1 = ZS-042 RTC Module
  LED2 = smd LED [color="Red (633nm)" package="0805 [SMD]"]

nets:
  N1: U1.D1, ZS-042_RTC1.SCL
  N2: U1.D2, ZS-042_RTC1.SDA
  N3: U1.D3, Part1.SDA
  N4: U1.D4, Part1.RST
  3V3: U1.3V3, Part1.3.3V, ZS-042_RTC1.VCC
  GND: U1.GND, J1.pin1, Part1.GND, LED1.cathode, ZS-042_RTC1.GND, LED2.cathode
  N5: U1.D5, Part1.SCK
  N6: U1.D6, Part1.MISO
  N7: U1.D7, Part1.MOSI
  N8: U1.D8, LED2.anode
  N9: U1.RX, LED1.anode
  N10: U1.TX, J1.pin2

custom parts:
  NodeMCU V3.0: ESP8266 based NodeMCU
  RFID-RC522-v2: A simple China made RFID-RC522 Reader; do check the pin labels, as this is a MFRC522 based clone.
