# Fritzing sketch Arduino_GSM (saved by Fritzing 0.9.3b)

parts:
  GSM_SIM_GPSR_SMS_SIM900_SIM1 = SIM800L [package=THT]
  Part1 = Arduino Uno (Rev3)
  LED1 = LED - 5mm [color="Green (555nm)" package="5 mm [THT]"]

nets:
  GND: GSM_SIM_GPSR_SMS_SIM900_SIM1.GND, Part1.GND, LED1.cathode
  N1: GSM_SIM_GPSR_SMS_SIM900_SIM1.SIM_TXD, Part1.D7
  N2: GSM_SIM_GPSR_SMS_SIM900_SIM1.SIM_RXD, Part1.D8
  N3: Part1.D13/SCK, LED1.anode

notes:
  Connect to a 12V DC Adapter
