# Fritzing sketch Arduino_GSM_MQ2_LM35 (saved by Fritzing 0.9.3b)
breadboards: 1

parts:
  T1 = LM35 Temperature Sensor [package="TO92 [THT]"]
  Part2 = Arduino Uno (Rev3)
  Part3 = MQ-2 LPG Gas Sensor [package=mq-2]
  GSM_SIM_GPSR_SMS_SIM900_SIM1 = SIM800L [package=THT]

nets:
  5V: T1.+Vs, Part2.5V, Part3.VCC
  N1: T1.Vout, Part2.A0
  GND: T1.GND, Part2.GND, Part3.GND, GSM_SIM_GPSR_SMS_SIM900_SIM1.GND
  N2: Part2.D8, GSM_SIM_GPSR_SMS_SIM900_SIM1.VDD, GSM_SIM_GPSR_SMS_SIM900_SIM1.SIM_RXD
  N3: Part2.D2, Part3.D0
  N4: Part2.D7, GSM_SIM_GPSR_SMS_SIM900_SIM1.SIM_TXD

notes:
  Connect to a 12V DC Adapter

custom parts:
  MQ-2 LPG Gas Sensor: MQ-2 Smoke LPG Butane Hydrogen Gas Sensor Detector Module
