# Fritzing sketch Arduino_pH (saved by Fritzing 0.9.3b)

parts:
  S2 = PH meter [package=THT]
  Part1 = Arduino Uno (Rev3)

nets:
  N1: S2.pin1, Part1.A0
  N2: S2.pin2, Part1.5V
  N3: S2.pin3, Part1.GND
