# Fritzing sketch ATtiny85_LED (saved by Fritzing 0.9.3b)
breadboards: 1

parts:
  U1 = attiny85 [package=dip]
  LED1 = LED - 5mm [color="Red (633nm)" package="5 mm [THT]"]
  U2 = Voltage Regulator - 5V [package="DPak [SMD]"]
  R2 = Resistor [tolerance=±5% resistance=1k package=THT]
  VCC1 = Battery block 9V
  C14 = Ceramic Capacitor [capacitance=100nF package="100 mil [THT, multilayer]"]
  C15 = Ceramic Capacitor [package="1206 [SMD, multilayer]"]

nets:
  N1: U1.Pin_3, LED1.anode
  N2: U1.Pin_4, U2.GND, R2.Pin_1, VCC1.-, C14.1, C15.0
  N3: U1.Pin_8, U2.output_voltage, C14.0
  N4: LED1.cathode, R2.Pin_0
  N5: U2.input_voltage, VCC1.+, C15.1

custom parts:
  Ceramic Capacitor: 330 nF multilayered Ceramic Capacitor
