# Fritzing sketch Arduino_ATtiny85 (saved by Fritzing 0.9.3b)
breadboards: 1

parts:
  Part2 = Arduino Uno (Rev3)
  U3 = attiny85 [package=dip]

nets:
  N1: Part2.D10_PWM/SS, U3.Pin_1
  N2: Part2.D11_PWM/MOSI, U3.Pin_5
  N3: Part2.D12/MISO, U3.Pin_6
  N4: Part2.D13/SCK, U3.Pin_7
  N5: Part2.5V, U3.Pin_8
  N6: Part2.GND, U3.Pin_4
