# Fritzing sketch ATtiny85_MPU6050_HC05 (saved by Fritzing 0.9.3b)
breadboards: 1

parts:
  U1 = ATTINY13 [package=dip]
  U2 = Voltage Regulator - 5V [package="TO220 [THT]"]
  C1 = Ceramic Capacitor [capacitance=100nF package="100 mil [THT, multilayer]"]
  GY2 = MPU-6050 Board GY-521 [form="♀ (female)" package=THT]
  Part2 = Bluetooth HC-05 Macho
  VCC1 = Battery block 9V
  C16 = Ceramic Capacitor [package="1206 [SMD, multilayer]"]

nets:
  N1: U1.PB3(ADC3), Part2.RXD
  GND: U1.GND, U2.GND, C1.0, GY2.pin2, GY2.pin7, Part2.GND, VCC1.-, C16.1
  N2: U1.PB0(MOSI), GY2.pin4
  N3: U1.PB2(SCK_ADC1), GY2.pin3
  VCC: U1.VCC, U2.output_voltage, C1.1, GY2.pin1, Part2.VCC
  N4: U2.input_voltage, VCC1.+, C16.0

custom parts:
  MPU-6050 Board GY-521: Acelerometro y Giroscopio MPU-6050 Board GY-521
  Ceramic Capacitor: 330 nF multilayered Ceramic Capacitor
