# Fritzing sketch ATtiny85_MPU6050_OLED (saved by Fritzing 0.9.3b)
breadboards: 1

parts:
  U4 = Voltage Regulator - 5V [package="TO220 [THT]"]
  C17 = Ceramic Capacitor [package="1206 [SMD, multilayer]"]
  VCC2 = Battery block 9V
  C18 = Ceramic Capacitor [capacitance=100nF package="100 mil [THT, multilayer]"]
  Squix1 = OLED 0.96" 128x64 I2C SSD1306
  U5 = ATTINY13 [package=dip]
  GY4 = MPU-6050 Board GY-521 [form="♀ (female)" package=THT]

nets:
  N1: U4.input_voltage, C17.0, VCC2.+
  GND: U4.GND, C17.1, VCC2.-, C18.0, Squix1.GND, U5.GND, GY4.pin2, GY4.pin7
  N2: U4.output_voltage, C18.1, Squix1.VCC, GY4.pin1
  N3: Squix1.SCL, U5.PB2(SCK_ADC1), GY4.pin3
  N4: Squix1.SCA, U5.PB0(MOSI), GY4.pin4

custom parts:
  Ceramic Capacitor: 330 nF multilayered Ceramic Capacitor
  MPU-6050 Board GY-521: Acelerometro y Giroscopio MPU-6050 Board GY-521
