# Fritzing sketch Receiver_Testing (saved by Fritzing 0.9.3b)

parts:
  Part4 = Arduino Uno (Rev3) - ICSP
  Part5 = Bluetooth HC-05 Macho

nets:
  N1: Part4.D0/RX, Part5.TXD
  N2: Part4.D1/TX, Part5.State
  5V: Part4.5V, Part5.VCC
  GND: Part4.GND, Part5.GND
