# Fritzing sketch Rpi_LED (saved by Fritzing 0.9.3b)

parts:
  Mod1 = Raspberry Pi 4B
  LED2 = smd LED [color="Red (633nm)" package="0603 [SMD]"]
  R2 = Resistor [tolerance=±5% resistance=220 package="2010 [SMD]"]

nets:
  N1: Mod1.GND, R2.Pin_1
  N2: Mod1.GPIO12, LED2.anode
  N3: LED2.cathode, R2.Pin_0
