# Fritzing sketch Pot_LED (saved by Fritzing 0.9.3b)
breadboards: 1

parts:
  R1 = Rotary Potentiometer (Small) [maximum_resistance=10kΩ package=THT]
  LED1 = LED - 3mm [color="Green (560nm)" package="3 mm [THT]"]
  VCC1 = Battery block 9V
  R2 = Resistor [tolerance=±5% resistance=220 package="2512 [SMD]"]

nets:
  N1: R1.leg1, VCC1.-
  N2: R1.wiper, R2.Pin_0
  N3: R1.leg2, LED1.cathode, VCC1.+
  N4: LED1.anode, R2.Pin_1
