# Fritzing sketch Pot_LED_MCU (saved by Fritzing 0.9.3b)
breadboards: 1

parts:
  R1 = Rotary Potentiometer (Small) [maximum_resistance=10kΩ package=THT]
  LED1 = LED - 3mm [color="Green (560nm)" package="3 mm [THT]"]
  R2 = Resistor [tolerance=±5% resistance=220 package="2512 [SMD]"]
  Part1 = Arduino Uno (Rev3)

nets:
  N1: R1.leg1, R2.Pin_0, Part1.GND
  N2: R1.wiper, Part1.A5/SCL
  N3: R1.leg2, Part1.5V
  N4: LED1.cathode, R2.Pin_1
  N5: LED1.anode, Part1.D6_PWM
