# Fritzing sketch Pot_Servo (saved by Fritzing 0.9.3b)
breadboards: 1

parts:
  Part1 = Arduino Uno (Rev3)
  R1 = Rotary Potentiometer (Small) [maximum_resistance=100kΩ package=THT]
  J1 = Basic Servo

nets:
  N1: Part1.A5/SCL, R1.wiper
  N2: Part1.D6_PWM, J1.pulse
  5V: Part1.5V, R1.leg1, J1.vcc
  GND: Part1.GND, R1.leg2, J1.gnd
