# Fritzing sketch Rpi_piCamera_servo (saved by Fritzing 0.9.3b)

parts:
  Mod1 = Raspberry Pi 4B
  J1 = Basic Servo
  IC1 = Rasberry Pi NIOR Camera [chip_label=IC package="DIP (Dual Inline) [THT]"]  # not connected

nets:
  5V: Mod1.5V, J1.vcc
  GND: Mod1.GND, J1.gnd
  N1: Mod1.GPIO18, J1.pulse

custom parts:
  Rasberry Pi NIOR Camera: Camera
