# Fritzing sketch HC05_Servo (saved by Fritzing 0.9.3b)

parts:
  Part1 = Arduino Uno (Rev3)
  J1 = Basic Servo
  Part2 = Bluetooth HC-05 Macho
  LED1 = LED - 5mm [color="Green (555nm)" package="5 mm [THT]"]
  LED2 = LED - 5mm [color="Red (635nm)" package="5 mm [THT]"]

nets:
  N1: Part1.D9_PWM, LED2.anode
  N2: Part1.D12/MISO, LED1.anode
  GND: Part1.GND, J1.gnd, Part2.GND, LED1.cathode, LED2.cathode
  N3: Part1.D0/RX, Part2.TXD
  N4: Part1.D1/TX, Part2.RXD
  N5: Part1.D5_PWM, J1.pulse
  3V3: Part1.3V3, J1.vcc
  5V: Part1.5V, Part2.VCC
