# Fritzing sketch FSR_LED (saved by Fritzing 0.9.3b)

parts:
  Part1 = Arduino Uno (Rev3)
  LED1 = LED - 5mm [color="Red (633nm)" package="5 mm [THT]"]
  J1 = Basic Force Sensing Resistor (FSR) [package=THT]
  R1 = Resistor [tolerance=±5% resistance=10k package=THT]

nets:
  N1: Part1.A0, J1.pin_0, R1.Pin_0
  N2: Part1.D11_PWM/MOSI, LED1.anode
  N3: Part1.GND, LED1.cathode, R1.Pin_1
  N4: Part1.5V, J1.pin_1
