# Fritzing sketch IR_Servo (saved by Fritzing 0.9.3b)

parts:
  Part1 = Arduino Uno (Rev3)
  J1 = Basic Servo
  M1 = fc-51 [package=THT]
  LED1 = LED - 3mm [color="Green (570nm)" package="3 mm [THT]"]

nets:
  N1: Part1.D11_PWM/MOSI, LED1.anode
  GND: Part1.GND, J1.gnd, M1.pin2, LED1.cathode
  N2: Part1.D2, M1.pin1
  N3: Part1.D5_PWM, J1.pulse
  3V3: Part1.3V3, J1.vcc
  N4: Part1.5V, M1.pin3
