# Fritzing sketch NodeMCU_GPS (saved by Fritzing 0.9.3b)

parts:
  Part1 = u-blox NEO-6M GPS Breakout
  U1 = NodeMCU V3.0

nets:
  GND: Part1.GND, U1.GND
  VCC: Part1.VCC, U1.3V3
  N1: Part1.TXD, U1.D5
  N2: Part1.RXD, U1.D6

custom parts:
  NodeMCU V3.0: ESP8266 based NodeMCU
