# Fritzing sketch TTL_GPS (saved by Fritzing 0.9.3b)

parts:
  Part1 = u-blox NEO-6M GPS Breakout
  USBUART1 = CP2102 USB UART Breakout

nets:
  GND: Part1.GND, USBUART1.GND
  N1: Part1.VCC, USBUART1.VCCIO
  N2: Part1.TXD, USBUART1.RXD
  N3: Part1.RXD, USBUART1.TXD

custom parts:
  CP2102 USB UART Breakout: CP2102 Usb Uart Breakout Board with Battery
