# Fritzing sketch NodeMCU_PIR (saved by Fritzing 0.9.3b)

parts:
  PIR1 = PIR sensor
  U1 = NodeMCU V3.0
  LED1 = smd LED [color="Red (633nm)" package="0805 [SMD]"]
  R1 = Resistor [tolerance=±5% resistance=220 package=THT]

nets:
  VDD: PIR1.VDD, U1.3V3
  N1: PIR1.SIG, U1.D6
  GND: PIR1.GND, U1.GND, R1.Pin_1
  N2: U1.D4, LED1.anode
  N3: LED1.cathode, R1.Pin_0

custom parts:
  NodeMCU V3.0: ESP8266 based NodeMCU
